# Fritzing sketch BalancingRobot_V3 (saved by Fritzing 0.9.3b)

parts:
  Part8 = InvenSense MPU6050
  U8 = SWITCH_SPDT [package=kps-1290]
  BATT3 = LiPoly Battery (1300mAh)
  SERVO1 = Tower Pro SG90 servo [part_number=101246]
  Part10 = Arduino Nano (Rev3.0)
  Pololu_A1 = Pololu A4988 [package=SO16]
  Pololu_A2 = Pololu A4988 [package=SO16]
  J1 = Basic Servo
  U9 = Mini-360 DC-DC Buck converter [package=THT]
  U10 = Mini-360 DC-DC Buck converter [package=THT]
  R2 = Resistor [tolerance=±5% resistance=330 package="1206 [SMD]"]
  Part11 = Bluetooth HC-05 Macho
  C1 = Electrolytic Capacitor [capacitance=100µF package="200 mil [THT, electrolytic]"]
  C2 = Electrolytic Capacitor [capacitance=100µF package="200 mil [THT, electrolytic]"]
  M5 = Stepper Motor - Bipolar
  M6 = Stepper Motor - Bipolar
  J3 = Buzzer
  Q2 = TRANSISTOR_NPN [package=to-92]

nets:
  VCC: Part8.VCC, Part10.5V, Pololu_A1.VDD, Pololu_A2.VDD, Part11.VCC
  GND: Part8.GND, SERVO1.GND, Part10.GND, Pololu_A1.GND#8, Pololu_A2.GND, J1.gnd, U9.OUT-, Part11.GND, C1.-, Q2.C
  N1: Part8.SCL, Part10.A5
  N2: Part8.SDA, Part10.A4
  N3: Part8.INT, Part10.D2
  N4: U8.P, BATT3.positive, Pololu_A1.VMOT, Pololu_A2.VMOT, U9.IN+, U10.IN+
  N5: U8.S, BATT3.negative, U9.IN-, U10.IN-, U10.OUT-
  N6: SERVO1.Signal, Part10.D9
  +5V: SERVO1.+5V, J1.vcc, U10.OUT+
  N7: Part10.D3, Pololu_A2.STEP
  N8: Part10.D4, Pololu_A2.DIR
  N9: Part10.D5, Pololu_A1.STEP
  N10: Part10.D6, Pololu_A1.DIR
  N11: Part10.D10, J1.pulse
  N12: Part10.VIN, U9.OUT+
  N13: Part10.A1, Part11.TXD
  N14: Part10.A0, Part11.RXD
  N15: Part10.3V3, J3.pin2
  N16: Part10.D13/SCK, R2.Pin_0
  N17: Pololu_A1.1B, M6.D
  N18: Pololu_A1.1A, M6.B
  N19: Pololu_A1.2A, M6.C
  N20: Pololu_A1.2B, M6.A
  N21: Pololu_A1.GND#14, C2.-
  N22: Pololu_A2.1B, M5.D
  N23: Pololu_A2.1A, M5.B
  N24: Pololu_A2.2A, M5.C
  N25: Pololu_A2.2B, M5.A
  N26: R2.Pin_1, Q2.B
  N27: C1.+, C2.+
  N28: J3.pin1, Q2.E

notes:
  - Arduino nano
  - ⁠⁠IMU MPI6050
  - ⁠Motor driver A4988
  - ⁠Motor stepper Nema17HS
  - Motor servo
  - ⁠Modul bluetooth HC05
  - ⁠Step down mini 360
  - ⁠Servo RDS3115
  - Buzzer
  - Kapasitor
  - Resistor 330 ohm
  - Push Button

custom parts:
  LiPoly Battery (1300mAh): Lithium Ion Polymer Battery (1300mAh)
  Tower Pro SG90 servo: Original file by John De Cristofaro http://www.adafruit.com/products/1449 Adafruit Feedback Servo (Small) Edited by: e-radionica.com 28/9/2015
  Mini-360 DC-DC Buck converter: Mini-360 DC-DC Buck converter. Tiny buck step down voltage converter, input voltage 4.75 to 23V output 1 to 17V adjustable. Available from ebay and the like.
  Buzzer: Fixed frequency buzzer
