# Fritzing sketch design fritz robotika balance (saved by Fritzing 0.9.3b)

parts:
  Part5 = Arduino Nano (Rev3.0) (ICSP)
  Part6 = InvenSense MPU6050
  U3 = ESP32-WROOM-32D-NodeMCU
  Part7 = Motor Driver 1A Dual TB6612FNG
  DC_Mot_Enc3 = DC Motor with two-phase hall-encoder [part_number=VT-E-G25A-06-177E]
  DC_Mot_Enc4 = DC Motor with two-phase hall-encoder [part_number=VT-E-G25A-06-177E]
  M3 = RioRand LM2596
  U4 = SWITCH_SPDT [package=kps-1290]
  BATT2 = LiPoly Battery (1300mAh)

nets:
  N1: Part5.D1/TX, U3.G16
  N2: Part5.D0/RX, U3.G17
  N3: Part5.D2, Part6.INT
  N4: Part5.VIN, Part7.VM, M3.Pin_3
  GND: Part5.GND, Part6.GND, U3.GND#13, DC_Mot_Enc3.pin5, DC_Mot_Enc4.pin5, M3.Pin_4
  5V: Part5.5V, Part6.VCC, U3.5V, DC_Mot_Enc3.pin2, DC_Mot_Enc4.pin2
  N5: Part5.A5, Part6.SCL
  N6: Part5.A4, Part6.SDA
  N7: U3.G27, DC_Mot_Enc4.pin4
  N8: U3.G14, DC_Mot_Enc4.pin3
  N9: U3.G12, DC_Mot_Enc3.pin4
  N10: U3.G13, DC_Mot_Enc3.pin3
  N11: U3.G15, Part7.PWMA
  N12: U3.G2, Part7.AIN2
  N13: U3.G4, Part7.AIN1
  N14: U3.G5, Part7.BIN1
  N15: U3.G18, Part7.BIN2
  N16: U3.G19, Part7.PWMB
  N17: U3.GND#50, Part7.GND
  N18: Part7.A02, DC_Mot_Enc3.pin6, DC_Mot_Enc4.pin6
  N19: Part7.A01, DC_Mot_Enc3.pin1, DC_Mot_Enc4.pin1
  N20: M3.Pin_1, BATT2.negative
  N21: M3.Pin_2, U4.S
  N22: U4.P, BATT2.positive

custom parts:
  LiPoly Battery (1300mAh): Lithium Ion Polymer Battery (1300mAh)
